# Fritzing sketch fritzing (saved by Fritzing 0.9.3b)
breadboards: 1

parts:
  Grove1 = Grove OLED 128x96
  Part1 = Photon
  R1 = Resistor [tolerance=±5% resistance=220 package="1206 [SMD]"]
  R2 = Resistor [tolerance=±5% resistance=220 package="1206 [SMD]"]

nets:
  GND: Grove1.GND, Part1.GND
  VCC: Grove1.VCC, Part1.VIN, R1.Pin_0, R2.Pin_0
  N1: Grove1.SDA, Part1.D0, R2.Pin_1
  N2: Grove1.SCL, Part1.D1, R1.Pin_1
